# Fritzing sketch PerfectDraftWifi (saved by Fritzing 0.9.9b)
breadboards: 1

parts:
  WeMos_D1_Mini1 = WeMos D1 Mini
  IC1 = Voltage Regulator [package=to220-igo]
  C1 = Capacitor Polarized [package=cpol-radial-100uf-25v]
  C2 = Capacitor Polarized [package=cpol-radial-100uf-25v]
  C3 = Ceramic Capacitor [capacitance=100nF voltage=35V package="100 mil [THT, multilayer]"]
  C4 = Ceramic Capacitor [capacitance=100nF voltage=35V package="100 mil [THT, multilayer]"]
  U1 = MCP41xxx [part_number=X9C103 package=so08]

nets:
  N1: WeMos_D1_Mini1.5V, WeMos_D1_Mini1.G, IC1.IN, IC1.OUT, C1.+, C1.-, C2.-, C3.1, C4.0, C4.1, U1.CS, U1.A
  N2: WeMos_D1_Mini1.D1, U1.W
  N3: WeMos_D1_Mini1.D2, U1.B
  N4: WeMos_D1_Mini1.D3, U1.VCC
  N5: IC1.GND, C2.+, C3.0

notes:
  GND VW VL VH
  UD INC CS VCC
  To NTC
  From Power Supply
  red/black
